// Logisim project 1607097_1607101_SAP1_Project.circ as structural Verilog: 12 circuits, main circuit main
module main (
  input  in_1,
  output [3:0] out_2,
  output [3:0] out_3,
  output [7:0] out_4,
  output [7:0] out_5
);

  wire Ce, CLK, clock_1_out, Cp, Ea, Ei, Ep, Eu, La, Lb, Li, Lm, Lo, n1607097_1607101_controller_1_hlt,
       not_1_out, not_2_out, not_3_out, not_4_out, not_5_out, not_6_out, not_7_out, not_8_out, not_9_out, Su;
  wire [3:0] Inst_Register_output0_3, Inst_Register_output4_7, MAR_output, Output_output, Output_output_2;
  wire [7:0] xor_7_out;

  not not_1 (not_1_out, Ce);
  not not_2 (not_2_out, CLK);
  not not_3 (not_3_out, Lm);
  not not_4 (not_4_out, Li);
  _1607097_Counter Program_Counter (.Output(out_3), .Cp(Cp), .CLK(not_2_out), .CLR(in_1), .Ep(Ep));
  _1607097_MAR MAR (.INPUT(out_3), .OUTPUT(MAR_output), .LOAD(not_3_out), .CLK(CLK), .CLR(in_1), .ENABLE(1'b1));
  _1607097_Inst_Reg Inst_Register (
    .Load(not_4_out), .CLK(CLK), .Input({out_2, out_3}), .Output4_7(Inst_Register_output4_7),
    .Output0_3(Inst_Register_output0_3), .Enable(1'b1), .CLR(in_1));
  _1607097_1607101_Controller u_1607097_1607101_controller_1 (
    .CLR(in_1), .I7_I4(Inst_Register_output4_7), .HLT(n1607097_1607101_controller_1_hlt), .Cp(Cp), .Ep(Ep),
    .LmB(Lm), .CeB(Ce), .LiB(Li), .EiB(Ei), .LaB(La), .Ea(Ea), .Su(Su), .Eu(Eu), .LbB(Lb), .LoB(Lo), .CLK(CLK));
  RAM #(.addrWidth(4)) ram_1 (.addr(MAR_output), .data({out_2, out_3}), .ld(not_1_out));  // open: sel, clk, clr
  not not_5 (not_5_out, Ei);
  assign out_3 = not_5_out ? Inst_Register_output0_3 : 4'bz;  // Controlled_Buffer controlled_buffer_1
  not not_6 (not_6_out, n1607097_1607101_controller_1_hlt);
  Clock clock_1 (.out(clock_1_out));
  assign CLK = not_6_out ? clock_1_out : 1'bz;  // Controlled_Buffer controlled_buffer_2
  assign {out_2, out_3} = Ea ? out_4 : 8'bz;  // Controlled_Buffer controlled_buffer_3
  _1607101_Register_A u_1607101_register_a_1 (
    .ENABLE(1'b1), .Clk(CLK), .Output(out_4), .LaB(not_9_out), .Input({out_2, out_3}));
  xor xor_1 (xor_7_out[6], Su, out_5[6]);
  xor xor_2 (xor_7_out[7], Su, out_5[7]);
  xor xor_3 (xor_7_out[5], Su, out_5[5]);
  xor xor_4 (xor_7_out[4], Su, out_5[4]);
  _1607101_Common_Register B (.Clk(CLK), .Output(out_5), .Load(not_7_out), .Input({out_2, out_3}));
  _1607101_Common_Register Output (
    .Clk(CLK), .Output({Output_output_2, Output_output}), .Load(not_8_out), .Input({out_2, out_3}));
  _1607101_Adder_Subtractor Adder__Subtractor (
    .A(out_4), .B(xor_7_out), .Cin(Su), .Output({out_2, out_3}), .Eu(Eu));  // open: Cout
  xor xor_5 (xor_7_out[3], Su, out_5[3]);
  xor xor_6 (xor_7_out[2], Su, out_5[2]);
  xor xor_7 (xor_7_out[0], Su, out_5[0]);
  xor xor_8 (xor_7_out[1], Su, out_5[1]);
  not not_7 (not_7_out, Lb);
  not not_8 (not_8_out, Lo);
  Hex_Digit_Display hex_digit_display_1 (.value(Output_output));  // open: dp
  Hex_Digit_Display hex_digit_display_2 (.value(Output_output_2));  // open: dp
  not not_9 (not_9_out, La);

  // Notes on the sheet:
  //   1607097
  //   SAP-1
  //   1607101
endmodule

module _1607097_Ring_Counter (
  input  CLK,
  input  CLR,
  output T6,
  output T5,
  output T4,
  output T3,
  output T2,
  output T1
);

  wire j_k_ff_1_qn, j_k_ff_2_qn, j_k_ff_3_qn, j_k_ff_4_qn, j_k_ff_5_qn, j_k_ff_6_q, not_1_out;

  J_K_Flip_Flop j_k_ff_1 (
    .J(T5), .clk(not_1_out), .K(j_k_ff_2_qn), .Q(T6), .Qn(j_k_ff_1_qn), .reset(CLR));  // open: preset, en
  J_K_Flip_Flop j_k_ff_2 (
    .J(T4), .clk(not_1_out), .K(j_k_ff_3_qn), .Q(T5), .Qn(j_k_ff_2_qn), .reset(CLR));  // open: preset, en
  J_K_Flip_Flop j_k_ff_3 (
    .J(T3), .clk(not_1_out), .K(j_k_ff_4_qn), .Q(T4), .Qn(j_k_ff_3_qn), .reset(CLR));  // open: preset, en
  J_K_Flip_Flop j_k_ff_4 (
    .J(T2), .clk(not_1_out), .K(j_k_ff_5_qn), .Q(T3), .Qn(j_k_ff_4_qn), .reset(CLR));  // open: preset, en
  J_K_Flip_Flop j_k_ff_5 (
    .J(T1), .clk(not_1_out), .K(j_k_ff_6_q), .Q(T2), .Qn(j_k_ff_5_qn), .reset(CLR));  // open: preset, en
  J_K_Flip_Flop j_k_ff_6 (
    .J(j_k_ff_1_qn), .clk(not_1_out), .K(T6), .Q(j_k_ff_6_q), .Qn(T1), .reset(CLR));  // open: preset, en
  not not_1 (not_1_out, CLK);

  // Notes on the sheet:
  //   1607097
  //   Ring Counter
endmodule

module _1607097_Decoder (
  input  I7,
  input  I6,
  input  I5,
  input  I4,
  output LDA,
  output ADD,
  output SUB,
  output OUT,
  output HLT
);

  wire and_1_out, and_2_out, and_3_out, and_4_out, not_1_out, not_2_out, not_3_out, not_4_out;

  not not_1 (not_1_out, I7);
  not not_2 (not_2_out, I6);
  not not_3 (not_3_out, I5);
  not not_4 (not_4_out, I4);
  and and_1 (and_1_out, not_1_out, not_2_out, not_3_out, not_4_out);
  and and_2 (and_2_out, not_1_out, not_2_out, not_3_out, I4);
  and and_3 (and_3_out, not_1_out, not_2_out, I5, not_4_out);
  and and_4 (and_4_out, I7, I6, I5, not_4_out);
  and and_5 (HLT, I7, I6, I5, I4);
  buf buffer_1 (LDA, and_1_out);
  buf buffer_2 (ADD, and_2_out);
  buf buffer_3 (SUB, and_3_out);
  buf buffer_4 (OUT, and_4_out);

  // Notes on the sheet:
  //   1607097
  //   Decoder
endmodule

module _1607097_Counter (
  input  Cp,
  input  CLK,
  input  CLR,
  input  Ep,
  output [3:0] Output
);

  wire j_k_ff_1_q, j_k_ff_2_q, j_k_ff_3_q, j_k_ff_4_q, not_1_out, not_2_out, not_3_out, not_4_out;

  assign Output[3] = Ep ? j_k_ff_1_q : 1'bz;  // Controlled_Buffer controlled_buffer_1
  assign Output[2] = Ep ? j_k_ff_2_q : 1'bz;  // Controlled_Buffer controlled_buffer_2
  not not_1 (not_1_out, j_k_ff_2_q);
  J_K_Flip_Flop j_k_ff_1 (.J(Cp), .clk(not_1_out), .K(Cp), .Q(j_k_ff_1_q), .reset(CLR));  // open: Qn, preset, en
  assign Output[1] = Ep ? j_k_ff_3_q : 1'bz;  // Controlled_Buffer controlled_buffer_3
  not not_2 (not_2_out, j_k_ff_3_q);
  J_K_Flip_Flop j_k_ff_2 (.J(Cp), .clk(not_2_out), .K(Cp), .Q(j_k_ff_2_q), .reset(CLR));  // open: Qn, preset, en
  assign Output[0] = Ep ? j_k_ff_4_q : 1'bz;  // Controlled_Buffer controlled_buffer_4
  not not_3 (not_3_out, j_k_ff_4_q);
  J_K_Flip_Flop j_k_ff_3 (.J(Cp), .clk(not_3_out), .K(Cp), .Q(j_k_ff_3_q), .reset(CLR));  // open: Qn, preset, en
  J_K_Flip_Flop j_k_ff_4 (.J(Cp), .clk(not_4_out), .K(Cp), .Q(j_k_ff_4_q), .reset(CLR));  // open: Qn, preset, en
  not not_4 (not_4_out, CLK);

  // Notes on the sheet:
  //   1607097
  //   Program Counter
endmodule

module _1607097_4bit_Reg (
  input  [3:0] Input,
  input  Load,
  input  CLK,
  input  CLR,
  input  Enable,
  output [3:0] Output
);

  wire and_1_out, and_2_out, and_3_out, and_4_out, and_5_out, and_6_out, and_7_out, and_8_out, d_ff_1_q,
       d_ff_2_q, d_ff_3_q, d_ff_4_q, not_1_out, or_1_out, or_2_out, or_3_out, or_4_out;

  and and_1 (and_1_out, d_ff_1_q, not_1_out);
  or or_1 (or_1_out, and_1_out, and_2_out);
  and and_2 (and_2_out, Input[3], Load);
  D_Flip_Flop d_ff_1 (.clk(CLK), .D(or_1_out), .Q(d_ff_1_q), .reset(CLR));  // open: Qn, preset, en
  assign Output[3] = Enable ? d_ff_1_q : 1'bz;  // Controlled_Buffer controlled_buffer_1
  and and_3 (and_3_out, d_ff_2_q, not_1_out);
  or or_2 (or_2_out, and_3_out, and_4_out);
  D_Flip_Flop d_ff_2 (.clk(CLK), .D(or_2_out), .Q(d_ff_2_q), .reset(CLR));  // open: Qn, preset, en
  assign Output[2] = Enable ? d_ff_2_q : 1'bz;  // Controlled_Buffer controlled_buffer_2
  and and_4 (and_4_out, Input[2], Load);
  and and_5 (and_5_out, d_ff_3_q, not_1_out);
  or or_3 (or_3_out, and_5_out, and_6_out);
  D_Flip_Flop d_ff_3 (.clk(CLK), .D(or_3_out), .Q(d_ff_3_q), .reset(CLR));  // open: Qn, preset, en
  and and_6 (and_6_out, Input[1], Load);
  assign Output[1] = Enable ? d_ff_3_q : 1'bz;  // Controlled_Buffer controlled_buffer_3
  and and_7 (and_7_out, d_ff_4_q, not_1_out);
  not not_1 (not_1_out, Load);
  and and_8 (and_8_out, Input[0], Load);
  or or_4 (or_4_out, and_7_out, and_8_out);
  D_Flip_Flop d_ff_4 (.clk(CLK), .D(or_4_out), .Q(d_ff_4_q), .reset(CLR));  // open: Qn, preset, en
  assign Output[0] = Enable ? d_ff_4_q : 1'bz;  // Controlled_Buffer controlled_buffer_4

  // Notes on the sheet:
  //   1607097
  //   4 bit Register
endmodule

// Controller
module _1607097_1607101_Controller (
  input  [3:0] I7_I4,
  input  CLR,
  input  CLK,
  output HLT,
  output Cp,
  output Ep,
  output LmB,
  output CeB,
  output LiB,
  output EiB,
  output LaB,
  output Ea,
  output Su,
  output Eu,
  output LbB,
  output LoB
);

  wire and_1_out, and_2_out, and_3_out, and_4_out, and_5_out, and_6_out, and_7_out, and_8_out, and_9_out,
       and_10_out, and_11_out, and_12_out, and_15_out, and_16_out, and_17_out, and_18_out,
       n1607097_decoder_1_add, n1607097_decoder_1_lda, n1607097_decoder_1_out, n1607097_decoder_1_sub,
       n1607097_ring_counter_1_t3, n1607097_ring_counter_1_t4, n1607097_ring_counter_1_t5,
       n1607097_ring_counter_1_t6, or_1_out, or_2_out, or_3_out, or_4_out, or_6_out;

  _1607097_Decoder u_1607097_decoder_1 (
    .I7(I7_I4[3]), .I6(I7_I4[2]), .I5(I7_I4[1]), .I4(I7_I4[0]), .LDA(n1607097_decoder_1_lda),
    .ADD(n1607097_decoder_1_add), .SUB(n1607097_decoder_1_sub), .OUT(n1607097_decoder_1_out), .HLT(HLT));
  and and_1 (and_1_out, n1607097_decoder_1_add, n1607097_ring_counter_1_t4);
  and and_2 (and_2_out, n1607097_decoder_1_lda, n1607097_ring_counter_1_t4);
  or or_1 (or_1_out, Ep, and_2_out, and_1_out, and_3_out);
  not not_1 (LmB, or_1_out);
  and and_3 (and_3_out, n1607097_decoder_1_sub, n1607097_ring_counter_1_t4);
  and and_4 (and_4_out, n1607097_decoder_1_lda, n1607097_ring_counter_1_t5);
  and and_5 (and_5_out, n1607097_decoder_1_add, n1607097_ring_counter_1_t5);
  or or_2 (or_2_out, n1607097_ring_counter_1_t3, and_4_out, and_5_out, and_6_out);
  not not_2 (CeB, or_2_out);
  and and_6 (and_6_out, n1607097_decoder_1_sub, n1607097_ring_counter_1_t5);
  not not_3 (LiB, n1607097_ring_counter_1_t3);
  and and_7 (and_7_out, n1607097_decoder_1_lda, n1607097_ring_counter_1_t4);
  and and_8 (and_8_out, n1607097_decoder_1_add, n1607097_ring_counter_1_t4);
  or or_3 (or_3_out, and_7_out, and_8_out, and_9_out);
  not not_4 (EiB, or_3_out);
  _1607097_Ring_Counter u_1607097_ring_counter_1 (
    .CLR(CLR), .T6(n1607097_ring_counter_1_t6), .T5(n1607097_ring_counter_1_t5),
    .T4(n1607097_ring_counter_1_t4), .T3(n1607097_ring_counter_1_t3), .T2(Cp), .T1(Ep), .CLK(CLK));
  and and_9 (and_9_out, n1607097_decoder_1_sub, n1607097_ring_counter_1_t4);
  and and_10 (and_10_out, n1607097_decoder_1_add, n1607097_ring_counter_1_t6);
  and and_11 (and_11_out, n1607097_decoder_1_lda, n1607097_ring_counter_1_t5);
  or or_4 (or_4_out, and_11_out, and_10_out, and_12_out);
  not not_5 (LaB, or_4_out);
  and and_12 (and_12_out, n1607097_decoder_1_sub, n1607097_ring_counter_1_t6);
  and and_13 (Ea, n1607097_decoder_1_out, n1607097_ring_counter_1_t4);
  and and_14 (Su, n1607097_decoder_1_sub, n1607097_ring_counter_1_t6);
  and and_15 (and_15_out, n1607097_decoder_1_sub, n1607097_ring_counter_1_t6);
  and and_16 (and_16_out, n1607097_decoder_1_add, n1607097_ring_counter_1_t6);
  or or_5 (Eu, and_16_out, and_15_out);
  and and_17 (and_17_out, n1607097_decoder_1_add, n1607097_ring_counter_1_t5);
  and and_18 (and_18_out, n1607097_decoder_1_sub, n1607097_ring_counter_1_t5);
  or or_6 (or_6_out, and_17_out, and_18_out);
  not not_6 (LbB, or_6_out);
  nand nand_1 (LoB, n1607097_decoder_1_out, n1607097_ring_counter_1_t4);

  // Notes on the sheet:
  //   1607097
  //   Controller
  //   1607101
  //   T6
  //   T5
  //   T4
  //   T3
  //   T2
  //   T1
  //   LDA
  //   ADD
  //   SUB
  //   OUT
endmodule

module _1607097_Inst_Reg (
  input  Load,
  input  CLK,
  input  [7:0] Input,
  input  Enable,
  input  CLR,
  output [3:0] Output4_7,
  output [3:0] Output0_3
);

  _1607097_4bit_Reg u_1607097_4bit_reg_1 (
    .Input(Input[7:4]), .Output(Output4_7), .Load(Load), .CLK(CLK), .CLR(CLR), .Enable(Enable));
  _1607097_4bit_Reg u_1607097_4bit_reg_2 (
    .Input(Input[3:0]), .Output(Output0_3), .Load(Load), .CLK(CLK), .CLR(CLR), .Enable(Enable));

  // Notes on the sheet:
  //   1607097
  //   Inst Register
endmodule

module _1607101_Adder_Subtractor (
  input  [7:0] A,
  input  [7:0] B,
  input  Cin,
  input  Eu,
  output Cout,
  output [7:0] Output
);

  wire n1607101_full_adder_1_cout, n1607101_full_adder_2_cout, n1607101_full_adder_3_cout,
       n1607101_full_adder_4_cout, n1607101_full_adder_5_cout, n1607101_full_adder_6_cout,
       n1607101_full_adder_7_cout;
  wire [7:0] n1607101_full_adder_1_s;

  assign Output = Eu ? n1607101_full_adder_1_s : 8'bz;  // Controlled_Buffer controlled_buffer_1
  _1607101_Full_Adder u_1607101_full_adder_1 (
    .A(A[0]), .B(B[0]), .Cin(Cin), .S(n1607101_full_adder_1_s[0]), .Cout(n1607101_full_adder_1_cout));
  _1607101_Full_Adder u_1607101_full_adder_2 (
    .A(A[1]), .B(B[1]), .Cin(n1607101_full_adder_1_cout), .S(n1607101_full_adder_1_s[1]),
    .Cout(n1607101_full_adder_2_cout));
  _1607101_Full_Adder u_1607101_full_adder_3 (
    .A(A[2]), .B(B[2]), .Cin(n1607101_full_adder_2_cout), .S(n1607101_full_adder_1_s[2]),
    .Cout(n1607101_full_adder_3_cout));
  _1607101_Full_Adder u_1607101_full_adder_4 (
    .A(A[3]), .B(B[3]), .Cin(n1607101_full_adder_3_cout), .S(n1607101_full_adder_1_s[3]),
    .Cout(n1607101_full_adder_4_cout));
  _1607101_Full_Adder u_1607101_full_adder_5 (
    .A(A[4]), .B(B[4]), .Cin(n1607101_full_adder_4_cout), .S(n1607101_full_adder_1_s[4]),
    .Cout(n1607101_full_adder_5_cout));
  _1607101_Full_Adder u_1607101_full_adder_6 (
    .A(A[5]), .B(B[5]), .Cin(n1607101_full_adder_5_cout), .S(n1607101_full_adder_1_s[5]),
    .Cout(n1607101_full_adder_6_cout));
  _1607101_Full_Adder u_1607101_full_adder_7 (
    .A(A[6]), .B(B[6]), .Cin(n1607101_full_adder_6_cout), .S(n1607101_full_adder_1_s[6]),
    .Cout(n1607101_full_adder_7_cout));
  _1607101_Full_Adder u_1607101_full_adder_8 (
    .A(A[7]), .B(B[7]), .Cin(n1607101_full_adder_7_cout), .S(n1607101_full_adder_1_s[7]), .Cout(Cout));

  // Notes on the sheet:
  //   Adder
  //   1607101
endmodule

// FA
module _1607101_Full_Adder (
  input  A,
  input  B,
  input  Cin,
  output S,
  output Cout
);

  wire and_1_out, and_2_out, xor_1_out;

  xor xor_1 (xor_1_out, A, B);
  xor xor_2 (S, xor_1_out, Cin);
  and and_1 (and_1_out, Cin, xor_1_out);
  and and_2 (and_2_out, B, A);
  or or_1 (Cout, and_1_out, and_2_out);

  // Notes on the sheet:
  //   Full Adder
  //   1607101
endmodule

// A
module _1607101_Register_A (
  input  LaB,
  input  [7:0] Input,
  input  ENABLE,
  input  Clk,
  output [7:0] Output
);

  wire and_1_out, and_2_out, and_3_out, and_4_out, and_5_out, and_6_out, and_7_out, and_8_out, and_9_out,
       and_10_out, and_11_out, and_12_out, and_13_out, and_14_out, and_15_out, and_16_out, d_ff_1_q,
       d_ff_2_q, d_ff_3_q, d_ff_4_q, d_ff_5_q, d_ff_6_q, d_ff_7_q, d_ff_8_q, not_1_out, or_1_out, or_2_out,
       or_3_out, or_4_out, or_5_out, or_6_out, or_7_out, or_8_out;

  and and_1 (and_1_out, LaB, Input[7]);
  and and_2 (and_2_out, not_1_out, d_ff_1_q);
  or or_1 (or_1_out, and_1_out, and_2_out);
  D_Flip_Flop d_ff_1 (.clk(Clk), .D(or_1_out), .Q(d_ff_1_q));  // open: Qn, preset, en, reset
  assign Output[7] = ENABLE ? d_ff_1_q : 1'bz;  // Controlled_Buffer controlled_buffer_1
  and and_3 (and_3_out, LaB, Input[6]);
  and and_4 (and_4_out, not_1_out, d_ff_2_q);
  or or_2 (or_2_out, and_3_out, and_4_out);
  D_Flip_Flop d_ff_2 (.clk(Clk), .D(or_2_out), .Q(d_ff_2_q));  // open: Qn, preset, en, reset
  assign Output[6] = ENABLE ? d_ff_2_q : 1'bz;  // Controlled_Buffer controlled_buffer_2
  and and_5 (and_5_out, LaB, Input[5]);
  or or_3 (or_3_out, and_5_out, and_6_out);
  and and_6 (and_6_out, not_1_out, d_ff_3_q);
  D_Flip_Flop d_ff_3 (.clk(Clk), .D(or_3_out), .Q(d_ff_3_q));  // open: Qn, preset, en, reset
  assign Output[5] = ENABLE ? d_ff_3_q : 1'bz;  // Controlled_Buffer controlled_buffer_3
  and and_7 (and_7_out, LaB, Input[4]);
  or or_4 (or_4_out, and_7_out, and_8_out);
  and and_8 (and_8_out, not_1_out, d_ff_4_q);
  D_Flip_Flop d_ff_4 (.clk(Clk), .D(or_4_out), .Q(d_ff_4_q));  // open: Qn, preset, en, reset
  and and_9 (and_9_out, LaB, Input[3]);
  or or_5 (or_5_out, and_9_out, and_10_out);
  assign Output[4] = ENABLE ? d_ff_4_q : 1'bz;  // Controlled_Buffer controlled_buffer_4
  and and_10 (and_10_out, not_1_out, d_ff_5_q);
  D_Flip_Flop d_ff_5 (.clk(Clk), .D(or_5_out), .Q(d_ff_5_q));  // open: Qn, preset, en, reset
  and and_11 (and_11_out, LaB, Input[2]);
  assign Output[3] = ENABLE ? d_ff_5_q : 1'bz;  // Controlled_Buffer controlled_buffer_5
  and and_12 (and_12_out, not_1_out, d_ff_6_q);
  or or_6 (or_6_out, and_11_out, and_12_out);
  D_Flip_Flop d_ff_6 (.clk(Clk), .D(or_6_out), .Q(d_ff_6_q));  // open: Qn, preset, en, reset
  assign Output[2] = ENABLE ? d_ff_6_q : 1'bz;  // Controlled_Buffer controlled_buffer_6
  and and_13 (and_13_out, LaB, Input[1]);
  and and_14 (and_14_out, not_1_out, d_ff_7_q);
  or or_7 (or_7_out, and_13_out, and_14_out);
  D_Flip_Flop d_ff_7 (.clk(Clk), .D(or_7_out), .Q(d_ff_7_q));  // open: Qn, preset, en, reset
  assign Output[1] = ENABLE ? d_ff_7_q : 1'bz;  // Controlled_Buffer controlled_buffer_7
  and and_15 (and_15_out, not_1_out, d_ff_8_q);
  and and_16 (and_16_out, LaB, Input[0]);
  or or_8 (or_8_out, and_16_out, and_15_out);
  not not_1 (not_1_out, LaB);
  D_Flip_Flop d_ff_8 (.clk(Clk), .D(or_8_out), .Q(d_ff_8_q));  // open: Qn, preset, en, reset
  assign Output[0] = ENABLE ? d_ff_8_q : 1'bz;  // Controlled_Buffer controlled_buffer_8

  // Notes on the sheet:
  //   Register A
  //   1607101
endmodule

module _1607101_Common_Register (
  input  Load,
  input  [7:0] Input,
  input  Clk,
  output [7:0] Output
);

  wire and_1_out, and_2_out, and_3_out, and_4_out, and_5_out, and_6_out, and_7_out, and_8_out, and_9_out,
       and_10_out, and_11_out, and_12_out, and_13_out, and_14_out, and_15_out, and_16_out, not_1_out,
       or_1_out, or_2_out, or_3_out, or_4_out, or_5_out, or_6_out, or_7_out, or_8_out;

  and and_1 (and_1_out, Load, Input[7]);
  and and_2 (and_2_out, not_1_out, Output[7]);
  or or_1 (or_1_out, and_1_out, and_2_out);
  D_Flip_Flop d_ff_1 (.clk(Clk), .D(or_1_out), .Q(Output[7]));  // open: Qn, preset, en, reset
  and and_3 (and_3_out, not_1_out, Output[6]);
  and and_4 (and_4_out, Load, Input[6]);
  or or_2 (or_2_out, and_4_out, and_3_out);
  D_Flip_Flop d_ff_2 (.clk(Clk), .D(or_2_out), .Q(Output[6]));  // open: Qn, preset, en, reset
  and and_5 (and_5_out, Load, Input[5]);
  and and_6 (and_6_out, not_1_out, Output[5]);
  or or_3 (or_3_out, and_5_out, and_6_out);
  D_Flip_Flop d_ff_3 (.clk(Clk), .D(or_3_out), .Q(Output[5]));  // open: Qn, preset, en, reset
  and and_7 (and_7_out, not_1_out, Output[4]);
  and and_8 (and_8_out, Load, Input[4]);
  or or_4 (or_4_out, and_8_out, and_7_out);
  D_Flip_Flop d_ff_4 (.clk(Clk), .D(or_4_out), .Q(Output[4]));  // open: Qn, preset, en, reset
  and and_9 (and_9_out, Load, Input[3]);
  and and_10 (and_10_out, not_1_out, Output[3]);
  or or_5 (or_5_out, and_9_out, and_10_out);
  D_Flip_Flop d_ff_5 (.clk(Clk), .D(or_5_out), .Q(Output[3]));  // open: Qn, preset, en, reset
  and and_11 (and_11_out, Load, Input[2]);
  or or_6 (or_6_out, and_11_out, and_12_out);
  and and_12 (and_12_out, not_1_out, Output[2]);
  D_Flip_Flop d_ff_6 (.clk(Clk), .D(or_6_out), .Q(Output[2]));  // open: Qn, preset, en, reset
  and and_13 (and_13_out, Load, Input[1]);
  and and_14 (and_14_out, not_1_out, Output[1]);
  or or_7 (or_7_out, and_13_out, and_14_out);
  D_Flip_Flop d_ff_7 (.clk(Clk), .D(or_7_out), .Q(Output[1]));  // open: Qn, preset, en, reset
  not not_1 (not_1_out, Load);
  and and_15 (and_15_out, not_1_out, Output[0]);
  and and_16 (and_16_out, Load, Input[0]);
  or or_8 (or_8_out, and_16_out, and_15_out);
  D_Flip_Flop d_ff_8 (.clk(Clk), .D(or_8_out), .Q(Output[0]));  // open: Qn, preset, en, reset

  // Notes on the sheet:
  //   1607101
  //   Common Register
endmodule

module _1607097_MAR (
  input  [3:0] INPUT,
  input  LOAD,
  input  CLK,
  input  CLR,
  input  ENABLE,
  output [3:0] OUTPUT
);

  wire and_1_out, and_2_out, and_3_out, and_4_out, and_5_out, and_6_out, and_7_out, and_8_out, d_ff_1_q,
       d_ff_2_q, d_ff_3_q, d_ff_4_q, not_1_out, or_1_out, or_2_out, or_3_out, or_4_out;

  and and_1 (and_1_out, d_ff_1_q, not_1_out);
  or or_1 (or_1_out, and_1_out, and_2_out);
  and and_2 (and_2_out, INPUT[3], LOAD);
  D_Flip_Flop d_ff_1 (.clk(CLK), .D(or_1_out), .Q(d_ff_1_q), .reset(CLR));  // open: Qn, preset, en
  assign OUTPUT[3] = ENABLE ? d_ff_1_q : 1'bz;  // Controlled_Buffer controlled_buffer_1
  and and_3 (and_3_out, d_ff_2_q, not_1_out);
  or or_2 (or_2_out, and_3_out, and_4_out);
  D_Flip_Flop d_ff_2 (.clk(CLK), .D(or_2_out), .Q(d_ff_2_q), .reset(CLR));  // open: Qn, preset, en
  assign OUTPUT[2] = ENABLE ? d_ff_2_q : 1'bz;  // Controlled_Buffer controlled_buffer_2
  and and_4 (and_4_out, INPUT[2], LOAD);
  and and_5 (and_5_out, d_ff_3_q, not_1_out);
  or or_3 (or_3_out, and_5_out, and_6_out);
  D_Flip_Flop d_ff_3 (.clk(CLK), .D(or_3_out), .Q(d_ff_3_q), .reset(CLR));  // open: Qn, preset, en
  and and_6 (and_6_out, INPUT[1], LOAD);
  assign OUTPUT[1] = ENABLE ? d_ff_3_q : 1'bz;  // Controlled_Buffer controlled_buffer_3
  and and_7 (and_7_out, d_ff_4_q, not_1_out);
  not not_1 (not_1_out, LOAD);
  and and_8 (and_8_out, INPUT[0], LOAD);
  or or_4 (or_4_out, and_7_out, and_8_out);
  D_Flip_Flop d_ff_4 (.clk(CLK), .D(or_4_out), .Q(d_ff_4_q), .reset(CLR));  // open: Qn, preset, en
  assign OUTPUT[0] = ENABLE ? d_ff_4_q : 1'bz;  // Controlled_Buffer controlled_buffer_4

  // Notes on the sheet:
  //   1607097
  //   MAR
endmodule
